// Logisim project 1.布尔逻辑.circ as structural Verilog: 1 circuit, main circuit main
module main (
  input  in_1,
  input  in_2,
  input  in_3,
  input  in_4,
  input  in_5,
  input  in_6,
  input  in_7,
  input  in_8,
  input  in_9,
  input  in_10,
  input  in_11,
  input  in_12,
  input  in_13,
  input  in_14,
  input  in_15,
  input  in_16,
  input  in_17,
  input  in_18,
  input  in_19,
  input  in_20,
  input  in_21,
  input  in_22,
  input  in_23,
  input  in_24,
  input  in_25,
  input  in_26,
  input  [1:0] in_27,
  input  in_28,
  output out_29,
  output out_30,
  output out_31,
  output out_32,
  output out_33,
  output out_34,
  output out_35,
  output out_36,
  output out_37,
  output out_38,
  output out_39,
  output out_40,
  output out_41,
  output out_42,
  output out_43,
  output out_44,
  output out_45,
  output out_46,
  output out_47,
  output out_48
);

  wire and_2_out, and_3_out, and_4_out, and_5_out, and_6_out, and_9_out, and_10_out, and_11_out, and_12_out,
       not_2_out, not_3_out, not_4_out, not_5_out, not_6_out, not_7_out, not_8_out, not_9_out;

  Demultiplexer demultiplexer_1 (.out0(out_37), .out1(out_39), .in(in_19), .sel(in_22));  // open: en
  Demultiplexer #(.select(2)) demultiplexer_2 (
    .out0(out_41), .out1(out_42), .out2(out_44), .out3(out_45), .in(in_25), .sel(in_27));  // open: en
  and And (out_29, in_1, in_3, in_3);
  or Or (out_32, in_6, in_7);
  xor Xor (out_34, in_9, in_10);
  Multiplexer multiplexer_1 (.in0(in_15), .in1(in_16), .out(out_36), .sel(in_17));  // open: en
  // OR_Gate or_2 is placed but not wired
  not Not (out_30, in_2);
  not not_2 (not_2_out, in_4);
  not not_3 (not_3_out, in_5);
  not not_4 (not_4_out, in_11);
  not not_5 (not_5_out, in_8);
  not not_6 (not_6_out, in_14);
  and and_2 (and_2_out, not_6_out, in_12);
  and and_3 (and_3_out, in_14, in_13);
  not not_7 (not_7_out, in_18);
  not not_8 (not_8_out, in_24);
  not not_9 (not_9_out, in_26);
  not not_10 (out_31, and_4_out);
  and and_4 (and_4_out, not_2_out, not_3_out);
  and and_5 (and_5_out, in_8, not_4_out);
  and and_6 (and_6_out, not_5_out, in_11);
  and and_7 (out_38, not_7_out, in_20);
  and and_8 (out_40, in_21, in_23);
  and and_9 (and_9_out, not_8_out, not_9_out);
  and and_10 (and_10_out, not_8_out, in_26);
  and and_11 (and_11_out, in_24, not_9_out);
  and and_12 (and_12_out, in_24, in_26);
  or or_3 (out_33, and_5_out, and_6_out);
  or or_4 (out_35, and_2_out, and_3_out);
  and and_13 (out_43, and_9_out, in_28);
  and and_14 (out_46, and_10_out, in_28);
  and and_15 (out_47, and_11_out, in_28);
  and and_16 (out_48, and_12_out, in_28);

  // Other names for the same wires on the sheet: a = in_4; b = in_5; Muxa = in_12; Muxb = in_13; Muxout = out_35;
  //   out = out_31; sel = in_14

  // Notes on the sheet:
  //   Xor(a,b)=Or(And(a,Not(b)),And(Not(a),b))
endmodule
